# Fritzing sketch IoTBox1 (saved by Fritzing 0.9.3b)
breadboards: 1

parts:
  Part1 = Photon
  Stepdown_Voltage1 = Polulu Stepdown Voltage [part_number=D24V25F3,D24V25F5]
  Power_plug1 = Power plug
  Grove1 = Grove Button
  Grove_LCD = Grove OLED 128x96
  R1 = Resistor [tolerance=±5% resistance=4.7k package="0402 [SMD]"]
  R2 = Resistor [tolerance=±5% resistance=4.7k package="0402 [SMD]"]
  Grove_Relay1 = Grove Relay
  L1 = Solenoid
  Grove_Buzzer1 = Grove Buzzer
  S1 = Toggle Switch [package=THT]
  R3 = Resistor [tolerance=±5% resistance=10k package="2512 [SMD]"]
  D1 = Diode [package=diode-1n4001]
  S2 = SWITCH-SPST-2 [package=r_sw_th]
  KEYPAD1 = Membrane Matrix Keypad
  IC1 = MCP23017 I2C I/O Expander

nets:
  GND: Part1.GND, Stepdown_Voltage1.GND, Power_plug1.GND, Grove1.GND, Grove_LCD.GND, Grove_Relay1.GND, Grove_Buzzer1.GND, R3.Pin_1, IC1.A0, IC1.A1, IC1.A2
  VIN: Part1.VIN, Stepdown_Voltage1.VIn, Grove_LCD.VCC, R1.Pin_0, R2.Pin_0, S2.P
  N1: Part1.D0, Grove_LCD.SDA, R1.Pin_1
  N2: Part1.D1, Grove_LCD.SCL, R2.Pin_1
  N3: Part1.D2, Grove1.SIG
  N4: Part1.D3, Grove_Buzzer1.SIG
  N5: Part1.D4, Grove_Relay1.SIG
  N6: Part1.D6, S1.L1, R3.Pin_0
  VCC: Part1.3V3, Grove1.VCC, Grove_Relay1.VCC, Grove_Buzzer1.VCC, S1.COM, IC1.RESET
  N7: Power_plug1.VCC, S2.O
  N8: L1.pin1, D1.A
  N9: L1.pin2, D1.C
  N10: KEYPAD1.1, IC1.GPA6
  N11: KEYPAD1.2, IC1.GPA5
  N12: KEYPAD1.3, IC1.GPA4
  N13: KEYPAD1.4, IC1.GPA3
  N14: KEYPAD1.5, IC1.GPA2
  N15: KEYPAD1.6, IC1.GPA1
  N16: KEYPAD1.7, IC1.GPA0

custom parts:
  Polulu Stepdown Voltage: Polulu Stepdown Voltage 3V3 or 5V, 2.5A
  Grove Relay: Relay, Grove connector.
  Grove Buzzer: Buzzer, Grove connector.
  Membrane Matrix Keypad: Membrane Matrix 3x4 Keypad
  MCP23017 I2C I/O Expander: The MCP23017 uses two i2c pins (these can be shared with other i2c devices), and in exchange gives you 16 general purpose pins. You can set each of 16 pins to be input, output, input with a pullup or open drain. There's even the ability to get an interrupt via an external pin when any of the inputs change so you don't have to keep polling the chip.
