# Fritzing sketch IoTBox_Perfboard (saved by Fritzing 0.9.3b)

parts:
  LCD = Header 4 [package=jst-4-pth]
  Buzzer = Header 4 [package=jst-4-pth]
  Part1 = Photon
  IC1 = MCP23017 I2C I/O Expander
  12V = Camdenboss CTB0158-2 [part_number=CTB0158-2 package=THT]
  LED = Header 4 [package=jst-4-pth]
  RELAY = Header 4 [package=jst-4-pth]
  I2C = Header 4 [package=jst-4-pth]
  Keypad = female pin header, 8 pins [form="♀ (female)"]
  SW1 = DIP Switch 8 Position [package=dipswitch-08]
  R1 = Resistor [tolerance=±5% resistance=10k package=THT]
  R2 = Resistor [tolerance=±5% resistance=10k package=THT]
  R3 = Resistor [tolerance=±5% resistance=10k package=THT]
  R4 = Resistor [tolerance=±5% resistance=220 package=THT]
  R5 = Resistor [tolerance=±5% resistance=220 package=THT]
  R6 = Resistor [tolerance=±5% resistance=220 package=THT]
  R7 = Resistor [tolerance=±5% resistance=220 package=THT]
  R8 = Resistor [tolerance=±5% resistance=220 package=THT]
  Solenoid = Camdenboss CTB0158-2 [part_number=CTB0158-2 package=THT]
  D1 = Schottky Diode [part_number=1N5817 breakdown_voltage=3.6V package="300 mil [THT]"]
  Relay = Camdenboss CTB0158-2 [part_number=CTB0158-2 package=THT]
  R9 = Resistor [tolerance=±5% resistance=220 package=THT]
  Keypad1 = female pin header, 2 pins [form="♀ (female)"]

nets:
  GND: LCD.1, Buzzer.1, Part1.GND, IC1.VSS, IC1.A0, IC1.A1, IC1.A2, LED.1, RELAY.1, I2C.1, R1.Pin_0, R2.Pin_0, R3.Pin_0, R4.Pin_0, R5.Pin_0, R6.Pin_0, R7.Pin_0, R8.Pin_0, R9.Pin_1
  VIN: LCD.2, Part1.VIN, IC1.VDD, IC1.RESET, LED.2, SW1.1, SW1.2, SW1.3, SW1.4, SW1.5, SW1.6, SW1.7, SW1.8, Keypad1.pin1
  N1: LCD.3, Part1.D0, IC1.SDA, I2C.3
  N2: LCD.4, Part1.D1, IC1.SCL, I2C.4
  N3: Buzzer.2, Part1.3V3, RELAY.2, I2C.2
  N4: Buzzer.4, Part1.D3
  N5: Part1.D5, R9.Pin_0, Keypad1.pin2
  N6: Part1.D6, LED.4
  N7: Part1.D7, LED.3
  N8: IC1.GPB0, SW1.16, R1.Pin_1
  N9: IC1.GPB1, SW1.15, R2.Pin_1
  N10: IC1.GPB2, SW1.14, R3.Pin_1
  N11: IC1.GPB3, SW1.13, R4.Pin_1
  N12: IC1.GPB4, SW1.12, R5.Pin_1
  N13: IC1.GPB5, SW1.11, R6.Pin_1
  N14: IC1.GPB6, SW1.10, R7.Pin_1
  N15: IC1.GPB7, SW1.9, R8.Pin_1
  N16: IC1.INTA, Keypad.pin8
  N17: IC1.GPA0, Keypad.pin7
  N18: IC1.GPA1, Keypad.pin6
  N19: IC1.GPA2, Keypad.pin5
  N20: IC1.GPA3, Keypad.pin4
  N21: IC1.GPA4, Keypad.pin3
  N22: IC1.GPA5, Keypad.pin2
  N23: IC1.GPA6, Keypad.pin1
  N24: 12V.pin1, Relay.pin1
  N25: 12V.pin2, Solenoid.pin2, D1.cathode
  N26: Solenoid.pin1, D1.anode, Relay.pin2

custom parts:
  MCP23017 I2C I/O Expander: The MCP23017 uses two i2c pins (these can be shared with other i2c devices), and in exchange gives you 16 general purpose pins. You can set each of 16 pins to be input, output, input with a pullup or open drain. There's even the ability to get an interrupt via an external pin when any of the inputs change so you don't have to keep polling the chip.
